# Fritzing sketch schematic (saved by Fritzing 0.9.4)

parts:
  M1 = Stepper Motor - Bipolar
  Raspberry_Pi_1 = Raspberry Pi 3 [part_number=RPI-3-V1.2]
  JACK1 = 2.1mm Barrel Jack with Terminal Block
  Mod1 = KY-024 Linear Hall Magnetic Sensor Module [package="Breakout board"]
  LED1 = LEDs [package=led10mm]
  RY1 = KF-301 Relay [package=THT]
  Pololu_A1 = Pololu A4988 [package=SO16]
  Part1 = 42CH Stepper Extension Board

nets:
  N1: M1.A, Part1.2B
  N2: M1.C, Part1.2A
  N3: M1.B, Part1.1B
  N4: M1.D, Part1.1A
  3V3: Raspberry_Pi_1.3v3, Raspberry_Pi_1.3V3, Mod1.+, Part1.DIR-V
  N5: Raspberry_Pi_1.GND, Mod1.G, RY1.ground, Pololu_A1.MS2, Part1.Driver_L3, Part1.DIR-G
  N6: Raspberry_Pi_1.GIPO6, RY1.signal
  N7: Raspberry_Pi_1.GIPO26, Mod1.D0
  N8: Raspberry_Pi_1.GIPO21, Part1.DIR-S
  N9: Raspberry_Pi_1.GIPO20, Part1.STEP-S
  N10: Raspberry_Pi_1.GIPO16, Part1.EN-S
  N11: JACK1.POS, RY1.C, Part1.VIN
  N12: JACK1.NEG, LED1.A, Part1.GND
  N13: LED1.C, RY1.NC
  N14: RY1.power, Part1.EN-V

custom parts:
  KY-024 Linear Hall Magnetic Sensor Module: KY-024 Linear Hall Magnetic Sensor Module reacts iin the presence of a magnetic field.
  KF-301 Relay: KF-301 SPDT Relay module using SRD-05VDC-SL-C relay.
  42CH Stepper Extension Board: Jolicobo 3D Printer 42CH Schrittmotortreiber Abchirmung Erweiterungskarte DRV8825 / A4988 UNO R3 (Schwarz)
